# Fritzing sketch DHT 11 (saved by Fritzing 0.8.7b)
circuit board: 8.94366cm x 5.64444cm
breadboards: 1

parts:
  Componente1 = Arduino Uno (Rev3)
  J1 = male pin header, 3 pins [form="♂ (male)"]
  R1 = Resistor [tolerance=±5% resistance=220 package=THT]
  U1 = LCD-16X2 [package=lcd-16x2]
  LED1 = LED - 5mm [color="Red (633nm)" package="5 mm [THT]"]

nets (from the breadboard view):
  N1: Componente1.D8, LED1.anode
  N2: Componente1.D11_PWM/MOSI, U1.E
  N3: Componente1.D12/MISO, U1.RS
  GND: Componente1.GND, U1.VSS, U1.R_W, LED1.cathode
  N4: Componente1.D2, R1.Pin_0
  N5: Componente1.D4, U1.DB7
  N6: Componente1.D5_PWM, U1.DB6
  N7: Componente1.D6_PWM, U1.DB5
  N8: Componente1.D7, U1.DB4
  N9: Componente1.5V, J1.pin1, U1.VO
  N10: J1.pin2, R1.Pin_1

notes:
  KY 015 Temperature and humidity sensor module
