# Fritzing sketch DHT 11 (saved by Fritzing 0.8.7b)
breadboards: 1

parts:
  Componente1 = Arduino Uno (Rev3)
  J1 = male pin header, 3 pins [form="♂ (male)"]
  R1 = Resistor [tolerance=±5% resistance=220 package=THT]
  U1 = LCD-16X2 [package=lcd-16x2]
  LED1 = LED - 5mm [color="Red (633nm)" package="5 mm [THT]"]
  BT1 = Bluetooth HC-06u [package=THT]
  J2 = Piezo Speaker
  R2 = Resistor [tolerance=±5% resistance=220 package=THT]

nets:
  N1: Componente1.D9_PWM, BT1.TXD
  N2: Componente1.D10_PWM/SS, J2.pin2
  N3: Componente1.D11_PWM/MOSI, U1.E
  N4: Componente1.D12/MISO, U1.RS
  N5: Componente1.D2, R1.Pin_0
  N6: Componente1.D3_PWM, BT1.RXD
  N7: Componente1.D4, U1.DB7
  N8: Componente1.D5_PWM, U1.DB6
  N9: Componente1.D6_PWM, U1.DB5
  N10: Componente1.D7, U1.DB4
  5V: Componente1.5V, J1.pin1, U1.VO, BT1.VCC
  GND: Componente1.GND, J1.pin3, U1.VSS, U1.R_W, LED1.cathode, BT1.GND, J2.pin1
  N11: J1.pin2, R1.Pin_1
  N12: LED1.anode, R2.Pin_0

notes:
  KY 015 Temperature and humidity sensor module

custom parts:
  Bluetooth HC-06u: Bluetooth HC-06 - face up, pins down 16.5mm x 37.5mm PCB
